# Fritzing sketch wiring-diagram (saved by Fritzing 0.9.2b)
breadboards: 1

parts:
  Part1 = Photon
  U1 = L9110 H-bridge module [part_number="L9110 H-bridge"]
  M1 = DC Motor
  M2 = DC Motor
  U3 = SWITCH-SPST-2 [package=switch-spst-vertical]
  VCC1 = 4 x AAA Battery Mount

nets (from the breadboard view):
  GND: Part1.GND, U1.GND, U3.O
  VIN: Part1.VIN, U1.VCC, VCC1.-
  N1: Part1.D0, U1.A-IB
  N2: Part1.D1, U1.A-IA
  N3: Part1.D2, U1.B-IB
  N4: Part1.D3, U1.B-IA
  N5: U1.MOTOR_A-A, M2.pin_2
  N6: U1.MOTOR_A-B, M2.pin_1
  N7: U1.MOTOR_B-A, M1.pin_2
  N8: U1.MOTOR_B-B, M1.pin_1
  N9: U3.P, VCC1.+

notes:
  Motor Controller wiring is reveresed in the diagram, because the board sits on the breadboard upside down.
